// Logisim project Sequential_8_bit_signed_multiplier.circ as structural Verilog: 20 circuits, main circuit main
module main (
  input  [7:0] Mutiplicand,
  input  [7:0] Mutiplier,
  output [15:0] out_3
);

  wire and_1_out, and_2_out, button_1_out, clock_1_out, clock_2_out, clock_3_out, d_ff_1_qn,
       decoder_7_segment_1_a_seg, decoder_7_segment_1_b_seg, decoder_7_segment_1_c_seg,
       decoder_7_segment_1_d_seg, decoder_7_segment_1_e_seg, decoder_7_segment_1_f_seg,
       decoder_7_segment_1_g_seg, decoder_7_segment_2_a_seg, decoder_7_segment_2_b_seg,
       decoder_7_segment_2_c_seg, decoder_7_segment_2_d_seg, decoder_7_segment_2_e_seg,
       decoder_7_segment_2_f_seg, decoder_7_segment_2_g_seg, decoder_7_segment_3_a_seg,
       decoder_7_segment_3_b_seg, decoder_7_segment_3_c_seg, decoder_7_segment_3_d_seg,
       decoder_7_segment_3_e_seg, decoder_7_segment_3_f_seg, decoder_7_segment_3_g_seg,
       finalproject_1_isnegetive, InitialLoad_out, not_1_out, or_1_out, shift_left_4_1_o0, shift_left_4_1_o1,
       shift_left_4_1_o2, shift_left_4_1_o3, shift_left_4_1_o4, shift_left_4_1_o5, shift_left_4_1_o6,
       shift_left_4_1_o7, shift_left_4_1_o8, shift_left_4_1_o9, shift_left_4_1_o10, shift_left_4_1_o11,
       shift_left_4_1_o12, shift_left_4_1_o13, shift_left_4_1_o14, shift_left_4_1_o15, shift_left_4_1_o16,
       shift_left_4_1_o17, shift_left_4_1_o18, shift_left_4_1_o19;
  wire [4:0] finalproject_1_counter;
  wire [19:0] finalproject_1_dicimal;

  Button InitialLoad (.out(InitialLoad_out));
  Clock clock_1 (.out(clock_1_out));
  _7_Segment_Display u_7_segment_display_1 (.g(finalproject_1_isnegetive));  // open: f, a, b, e, d, c, dp
  D_Flip_Flop d_ff_1 (.D(button_1_out), .clk(clock_2_out), .Qn(d_ff_1_qn));  // open: Q, preset, reset
  Button button_1 (.out(button_1_out));
  Clock clock_2 (.out(clock_2_out));
  _7_Segment_Display u_7_segment_display_2 (
    .g(decoder_7_segment_1_g_seg), .f(decoder_7_segment_1_f_seg), .a(decoder_7_segment_1_a_seg),
    .b(decoder_7_segment_1_b_seg), .e(decoder_7_segment_1_e_seg), .d(decoder_7_segment_1_d_seg),
    .c(decoder_7_segment_1_c_seg));  // open: dp
  finalProject finalproject_1 (
    .InitialLoad(InitialLoad_out), .Multiplicand(Mutiplicand), .Multiplier(Mutiplier), .Clock(clock_1_out),
    .ProductInBinary(out_3), .Dicimal(finalproject_1_dicimal), .IsNegetive(finalproject_1_isnegetive),
    .counter(finalproject_1_counter));
  and and_1 (and_1_out, button_1_out, d_ff_1_qn);
  Decoder_7_segment decoder_7_segment_1 (
    .d(shift_left_4_1_o16), .c(shift_left_4_1_o17), .b(shift_left_4_1_o18), .a(shift_left_4_1_o19),
    .A_seg(decoder_7_segment_1_a_seg), .B_seg(decoder_7_segment_1_b_seg), .C_seg(decoder_7_segment_1_c_seg),
    .D_seg(decoder_7_segment_1_d_seg), .E_seg(decoder_7_segment_1_e_seg), .F_seg(decoder_7_segment_1_f_seg),
    .G_seg(decoder_7_segment_1_g_seg));
  and and_2 (and_2_out, finalproject_1_counter[4], not_1_out);
  _7_Segment_Display u_7_segment_display_3 (
    .g(decoder_7_segment_2_g_seg), .f(decoder_7_segment_2_f_seg), .a(decoder_7_segment_2_a_seg),
    .b(decoder_7_segment_2_b_seg), .e(decoder_7_segment_2_e_seg), .d(decoder_7_segment_2_d_seg),
    .c(decoder_7_segment_2_c_seg));  // open: dp
  Clock clock_3 (.out(clock_3_out));
  Decoder_7_segment decoder_7_segment_2 (
    .d(shift_left_4_1_o12), .c(shift_left_4_1_o13), .b(shift_left_4_1_o14), .a(shift_left_4_1_o15),
    .A_seg(decoder_7_segment_2_a_seg), .B_seg(decoder_7_segment_2_b_seg), .C_seg(decoder_7_segment_2_c_seg),
    .D_seg(decoder_7_segment_2_d_seg), .E_seg(decoder_7_segment_2_e_seg), .F_seg(decoder_7_segment_2_f_seg),
    .G_seg(decoder_7_segment_2_g_seg));
  _7_Segment_Display u_7_segment_display_4 (
    .g(decoder_7_segment_3_g_seg), .f(decoder_7_segment_3_f_seg), .a(decoder_7_segment_3_a_seg),
    .b(decoder_7_segment_3_b_seg), .e(decoder_7_segment_3_e_seg), .d(decoder_7_segment_3_d_seg),
    .c(decoder_7_segment_3_c_seg));  // open: dp
  Decoder_7_segment decoder_7_segment_3 (
    .d(shift_left_4_1_o8), .c(shift_left_4_1_o9), .b(shift_left_4_1_o10), .a(shift_left_4_1_o11),
    .A_seg(decoder_7_segment_3_a_seg), .B_seg(decoder_7_segment_3_b_seg), .C_seg(decoder_7_segment_3_c_seg),
    .D_seg(decoder_7_segment_3_d_seg), .E_seg(decoder_7_segment_3_e_seg), .F_seg(decoder_7_segment_3_f_seg),
    .G_seg(decoder_7_segment_3_g_seg));
  shift_left_4 shift_left_4_1 (
    .a0(finalproject_1_dicimal[0]), .a1(finalproject_1_dicimal[1]), .a2(finalproject_1_dicimal[2]),
    .a3(finalproject_1_dicimal[3]), .a4(finalproject_1_dicimal[4]), .a5(finalproject_1_dicimal[5]),
    .a6(finalproject_1_dicimal[6]), .a7(finalproject_1_dicimal[7]), .a8(finalproject_1_dicimal[8]),
    .a9(finalproject_1_dicimal[9]), .a10(finalproject_1_dicimal[10]), .a11(finalproject_1_dicimal[11]),
    .a12(finalproject_1_dicimal[12]), .a13(finalproject_1_dicimal[13]), .a14(finalproject_1_dicimal[14]),
    .a15(finalproject_1_dicimal[15]), .a16(finalproject_1_dicimal[16]), .a17(finalproject_1_dicimal[17]),
    .a18(finalproject_1_dicimal[18]), .a19(finalproject_1_dicimal[19]), .clk(clock_3_out), .load(and_2_out),
    .enable(and_1_out), .o0(shift_left_4_1_o0), .o1(shift_left_4_1_o1), .o2(shift_left_4_1_o2),
    .o3(shift_left_4_1_o3), .o4(shift_left_4_1_o4), .o5(shift_left_4_1_o5), .o6(shift_left_4_1_o6),
    .o7(shift_left_4_1_o7), .o8(shift_left_4_1_o8), .o9(shift_left_4_1_o9), .o10(shift_left_4_1_o10),
    .o11(shift_left_4_1_o11), .o12(shift_left_4_1_o12), .o13(shift_left_4_1_o13), .o14(shift_left_4_1_o14),
    .o15(shift_left_4_1_o15), .o16(shift_left_4_1_o16), .o17(shift_left_4_1_o17), .o18(shift_left_4_1_o18),
    .o19(shift_left_4_1_o19));
  not not_1 (not_1_out, or_1_out);
  or or_1 (or_1_out, shift_left_4_1_o0, shift_left_4_1_o1, shift_left_4_1_o2, shift_left_4_1_o3, shift_left_4_1_o4, shift_left_4_1_o5, shift_left_4_1_o6, shift_left_4_1_o7, shift_left_4_1_o8, shift_left_4_1_o9, shift_left_4_1_o10, shift_left_4_1_o11, shift_left_4_1_o12, shift_left_4_1_o13, shift_left_4_1_o14, shift_left_4_1_o15, shift_left_4_1_o16, shift_left_4_1_o17, shift_left_4_1_o18, shift_left_4_1_o19);
endmodule

module unsignedMultiplier (
  input  [7:0] Multiplier,
  input  [7:0] Multiplicand,
  input  Clock,
  input  Initial_constant,
  output [15:0] Product,
  output Finished
);

  wire and_1_out, d_ff_1_q, d_ff_2_q, d_ff_2_qn, multiplexer_1_out, not_1_out, not_2_out, or_1_out, or_2_out;
  wire [7:0] b8bitshiftright_1_q0, multiplexer_4_out;
  wire [15:0] b16bitfulladder_1_s0, b16bitshiftleft_1_q0, multiplexer_2_out, multiplexer_3_out;

  Multiplexer multiplexer_1 (.in0(multiplexer_4_out[0]), .in1(1'b0), .out(multiplexer_1_out), .sel(and_1_out));
  not not_1 (not_1_out, d_ff_2_q);
  or or_1 (or_1_out, not_1_out, d_ff_1_q);
  D_Flip_Flop d_ff_1 (.D(or_1_out), .clk(Clock), .Q(d_ff_1_q));  // open: Qn, preset, reset
  Multiplexer #(.width(16)) multiplexer_2 (
    .in0({{8{1'b0}}, Multiplicand}), .in1(b16bitshiftleft_1_q0), .out(multiplexer_2_out), .sel(d_ff_1_q));
  Multiplexer #(.width(16)) multiplexer_3 (
    .in0(Product), .in1(b16bitfulladder_1_s0), .out(multiplexer_3_out), .sel(multiplexer_1_out));
  Multiplexer #(.width(8)) multiplexer_4 (
    .in0(Multiplier), .in1(b8bitshiftright_1_q0), .out(multiplexer_4_out), .sel(d_ff_1_q));
  or or_2 (or_2_out, multiplexer_4_out[7], multiplexer_4_out[6], multiplexer_4_out[5], multiplexer_4_out[4], multiplexer_4_out[3], multiplexer_4_out[2], multiplexer_4_out[1], multiplexer_4_out[0]);
  not not_2 (not_2_out, d_ff_2_q);
  and and_1 (and_1_out, not_2_out, not_1_out);
  B16_bitRegister b16_bitregister_1 (
    .d0(multiplexer_3_out[0]), .d1(multiplexer_3_out[1]), .d2(multiplexer_3_out[2]),
    .d3(multiplexer_3_out[3]), .d4(multiplexer_3_out[4]), .d5(multiplexer_3_out[5]),
    .d6(multiplexer_3_out[6]), .d7(multiplexer_3_out[7]), .d8(multiplexer_3_out[8]),
    .d9(multiplexer_3_out[9]), .d10(multiplexer_3_out[10]), .d11(multiplexer_3_out[11]),
    .d12(multiplexer_3_out[12]), .d13(multiplexer_3_out[13]), .d14(multiplexer_3_out[14]),
    .d15(multiplexer_3_out[15]), .Clock(Clock), .q0(Product[0]), .q1(Product[1]), .q2(Product[2]),
    .q3(Product[3]), .q4(Product[4]), .q5(Product[5]), .q6(Product[6]), .q7(Product[7]), .q8(Product[8]),
    .q9(Product[9]), .q10(Product[10]), .q11(Product[11]), .q12(Product[12]), .q13(Product[13]),
    .q14(Product[14]), .q15(Product[15]));
  B8bitShiftRight b8bitshiftright_1 (
    .Clock(Clock), .s0(d_ff_2_q), .s1(not_1_out), .d0(multiplexer_4_out[0]), .d1(multiplexer_4_out[1]),
    .d2(multiplexer_4_out[2]), .d3(multiplexer_4_out[3]), .d4(multiplexer_4_out[4]),
    .d5(multiplexer_4_out[5]), .d6(multiplexer_4_out[6]), .d7(multiplexer_4_out[7]),
    .q0(b8bitshiftright_1_q0[0]), .q1(b8bitshiftright_1_q0[1]), .q2(b8bitshiftright_1_q0[2]),
    .q3(b8bitshiftright_1_q0[3]), .q4(b8bitshiftright_1_q0[4]), .q5(b8bitshiftright_1_q0[5]),
    .q6(b8bitshiftright_1_q0[6]), .q7(b8bitshiftright_1_q0[7]));
  not not_3 (Finished, or_2_out);
  D_Flip_Flop d_ff_2 (
    .D(d_ff_2_qn), .clk(Clock), .Q(d_ff_2_q), .Qn(d_ff_2_qn), .preset(Initial_constant));  // open: reset
  B16bitShiftLeft b16bitshiftleft_1 (
    .Clock(Clock), .s0(d_ff_2_q), .s1(not_1_out), .d0(multiplexer_2_out[0]), .d1(multiplexer_2_out[1]),
    .d2(multiplexer_2_out[2]), .d3(multiplexer_2_out[3]), .d4(multiplexer_2_out[4]),
    .d5(multiplexer_2_out[5]), .d6(multiplexer_2_out[6]), .d7(multiplexer_2_out[7]),
    .d8(multiplexer_2_out[8]), .d9(multiplexer_2_out[9]), .d10(multiplexer_2_out[10]),
    .d11(multiplexer_2_out[11]), .d12(multiplexer_2_out[12]), .d13(multiplexer_2_out[13]),
    .d14(multiplexer_2_out[14]), .d15(multiplexer_2_out[15]), .q0(b16bitshiftleft_1_q0[0]),
    .q1(b16bitshiftleft_1_q0[1]), .q2(b16bitshiftleft_1_q0[2]), .q3(b16bitshiftleft_1_q0[3]),
    .q4(b16bitshiftleft_1_q0[4]), .q5(b16bitshiftleft_1_q0[5]), .q6(b16bitshiftleft_1_q0[6]),
    .q7(b16bitshiftleft_1_q0[7]), .q8(b16bitshiftleft_1_q0[8]), .q9(b16bitshiftleft_1_q0[9]),
    .q10(b16bitshiftleft_1_q0[10]), .q11(b16bitshiftleft_1_q0[11]), .q12(b16bitshiftleft_1_q0[12]),
    .q13(b16bitshiftleft_1_q0[13]), .q14(b16bitshiftleft_1_q0[14]), .q15(b16bitshiftleft_1_q0[15]));
  B16bitFullAdder b16bitfulladder_1 (
    .cin(1'b0), .a0(multiplexer_2_out[0]), .a1(multiplexer_2_out[1]), .a2(multiplexer_2_out[2]),
    .a3(multiplexer_2_out[3]), .a4(multiplexer_2_out[4]), .a5(multiplexer_2_out[5]),
    .a6(multiplexer_2_out[6]), .a7(multiplexer_2_out[7]), .a8(multiplexer_2_out[8]),
    .a9(multiplexer_2_out[9]), .a10(multiplexer_2_out[10]), .a11(multiplexer_2_out[11]),
    .a12(multiplexer_2_out[12]), .a13(multiplexer_2_out[13]), .a14(multiplexer_2_out[14]),
    .a15(multiplexer_2_out[15]), .b0(Product[0]), .b1(Product[1]), .b2(Product[2]), .b3(Product[3]),
    .b4(Product[4]), .b5(Product[5]), .b6(Product[6]), .b7(Product[7]), .b8(Product[8]), .b9(Product[9]),
    .b10(Product[10]), .b11(Product[11]), .b12(Product[12]), .b13(Product[13]), .b14(Product[14]),
    .b15(Product[15]), .s0(b16bitfulladder_1_s0[0]), .s1(b16bitfulladder_1_s0[1]),
    .s2(b16bitfulladder_1_s0[2]), .s3(b16bitfulladder_1_s0[3]), .s4(b16bitfulladder_1_s0[4]),
    .s5(b16bitfulladder_1_s0[5]), .s6(b16bitfulladder_1_s0[6]), .s7(b16bitfulladder_1_s0[7]),
    .s8(b16bitfulladder_1_s0[8]), .s9(b16bitfulladder_1_s0[9]), .s10(b16bitfulladder_1_s0[10]),
    .s11(b16bitfulladder_1_s0[11]), .s12(b16bitfulladder_1_s0[12]), .s13(b16bitfulladder_1_s0[13]),
    .s14(b16bitfulladder_1_s0[14]), .s15(b16bitfulladder_1_s0[15]));  // open: cout
endmodule

module B8_bitRegister (
  input  d0,
  input  d1,
  input  d2,
  input  d3,
  input  d4,
  input  d5,
  input  d6,
  input  d7,
  input  Clock,
  output q0,
  output q1,
  output q2,
  output q3,
  output q4,
  output q5,
  output q6,
  output q7
);

  D_Flip_Flop d_ff_1 (.D(d0), .clk(Clock), .Q(q0));  // open: Qn, preset, reset
  D_Flip_Flop d_ff_2 (.D(d1), .clk(Clock), .Q(q1));  // open: Qn, preset, reset
  D_Flip_Flop d_ff_3 (.D(d2), .clk(Clock), .Q(q2));  // open: Qn, preset, reset
  D_Flip_Flop d_ff_4 (.D(d3), .clk(Clock), .Q(q3));  // open: Qn, preset, reset
  D_Flip_Flop d_ff_5 (.D(d4), .clk(Clock), .Q(q4));  // open: Qn, preset, reset
  D_Flip_Flop d_ff_6 (.D(d5), .clk(Clock), .Q(q5));  // open: Qn, preset, reset
  D_Flip_Flop d_ff_7 (.D(d6), .clk(Clock), .Q(q6));  // open: Qn, preset, reset
  D_Flip_Flop d_ff_8 (.D(d7), .clk(Clock), .Q(q7));  // open: Qn, preset, reset
endmodule

module B16_bitRegister (
  input  d0,
  input  d1,
  input  d2,
  input  d3,
  input  d4,
  input  d5,
  input  d6,
  input  d7,
  input  d8,
  input  d9,
  input  d10,
  input  d11,
  input  d12,
  input  d13,
  input  d14,
  input  d15,
  input  Clock,
  output q0,
  output q1,
  output q2,
  output q3,
  output q4,
  output q5,
  output q6,
  output q7,
  output q8,
  output q9,
  output q10,
  output q11,
  output q12,
  output q13,
  output q14,
  output q15
);

  D_Flip_Flop d_ff_1 (.D(d0), .clk(Clock), .Q(q0));  // open: Qn, preset, reset
  D_Flip_Flop d_ff_2 (.D(d1), .clk(Clock), .Q(q1));  // open: Qn, preset, reset
  D_Flip_Flop d_ff_3 (.D(d2), .clk(Clock), .Q(q2));  // open: Qn, preset, reset
  D_Flip_Flop d_ff_4 (.D(d3), .clk(Clock), .Q(q3));  // open: Qn, preset, reset
  D_Flip_Flop d_ff_5 (.D(d4), .clk(Clock), .Q(q4));  // open: Qn, preset, reset
  D_Flip_Flop d_ff_6 (.D(d5), .clk(Clock), .Q(q5));  // open: Qn, preset, reset
  D_Flip_Flop d_ff_7 (.D(d6), .clk(Clock), .Q(q6));  // open: Qn, preset, reset
  D_Flip_Flop d_ff_8 (.D(d7), .clk(Clock), .Q(q7));  // open: Qn, preset, reset
  D_Flip_Flop d_ff_9 (.D(d8), .clk(Clock), .Q(q8));  // open: Qn, preset, reset
  D_Flip_Flop d_ff_10 (.D(d9), .clk(Clock), .Q(q9));  // open: Qn, preset, reset
  D_Flip_Flop d_ff_11 (.D(d10), .clk(Clock), .Q(q10));  // open: Qn, preset, reset
  D_Flip_Flop d_ff_12 (.D(d11), .clk(Clock), .Q(q11));  // open: Qn, preset, reset
  D_Flip_Flop d_ff_13 (.D(d12), .clk(Clock), .Q(q12));  // open: Qn, preset, reset
  D_Flip_Flop d_ff_14 (.D(d13), .clk(Clock), .Q(q13));  // open: Qn, preset, reset
  D_Flip_Flop d_ff_15 (.D(d14), .clk(Clock), .Q(q14));  // open: Qn, preset, reset
  D_Flip_Flop d_ff_16 (.D(d15), .clk(Clock), .Q(q15));  // open: Qn, preset, reset
endmodule

module B16bitFullAdder (
  input  cin,
  input  a0,
  input  a1,
  input  a2,
  input  a3,
  input  a4,
  input  a5,
  input  a6,
  input  a7,
  input  a8,
  input  a9,
  input  a10,
  input  a11,
  input  a12,
  input  a13,
  input  a14,
  input  a15,
  input  b0,
  input  b1,
  input  b2,
  input  b3,
  input  b4,
  input  b5,
  input  b6,
  input  b7,
  input  b8,
  input  b9,
  input  b10,
  input  b11,
  input  b12,
  input  b13,
  input  b14,
  input  b15,
  output s0,
  output s1,
  output s2,
  output s3,
  output s4,
  output s5,
  output s6,
  output s7,
  output s8,
  output s9,
  output s10,
  output s11,
  output s12,
  output s13,
  output s14,
  output s15,
  output cout
);

  wire fa_1_cout, fa_2_cout, fa_3_cout, fa_4_cout, fa_5_cout, fa_6_cout, fa_7_cout, fa_8_cout, fa_9_cout,
       fa_10_cout, fa_11_cout, fa_12_cout, fa_13_cout, fa_14_cout, fa_15_cout;

  FA fa_1 (.cin(cin), .a(a0), .b(b0), .s(s0), .Cout(fa_1_cout));
  FA fa_2 (.cin(fa_1_cout), .a(a1), .b(b1), .s(s1), .Cout(fa_2_cout));
  FA fa_3 (.cin(fa_2_cout), .a(a2), .b(b2), .s(s2), .Cout(fa_3_cout));
  FA fa_4 (.cin(fa_3_cout), .a(a3), .b(b3), .s(s3), .Cout(fa_4_cout));
  FA fa_5 (.cin(fa_4_cout), .a(a4), .b(b4), .s(s4), .Cout(fa_5_cout));
  FA fa_6 (.cin(fa_5_cout), .a(a5), .b(b5), .s(s5), .Cout(fa_6_cout));
  FA fa_7 (.cin(fa_6_cout), .a(a6), .b(b6), .s(s6), .Cout(fa_7_cout));
  FA fa_8 (.cin(fa_7_cout), .a(a7), .b(b7), .s(s7), .Cout(fa_8_cout));
  FA fa_9 (.cin(fa_8_cout), .a(a8), .b(b8), .s(s8), .Cout(fa_9_cout));
  FA fa_10 (.cin(fa_9_cout), .a(a9), .b(b9), .s(s9), .Cout(fa_10_cout));
  FA fa_11 (.cin(fa_10_cout), .a(a10), .b(b10), .s(s10), .Cout(fa_11_cout));
  FA fa_12 (.cin(fa_11_cout), .a(a11), .b(b11), .s(s11), .Cout(fa_12_cout));
  FA fa_13 (.cin(fa_12_cout), .a(a12), .b(b12), .s(s12), .Cout(fa_13_cout));
  FA fa_14 (.cin(fa_13_cout), .a(a13), .b(b13), .s(s13), .Cout(fa_14_cout));
  FA fa_15 (.cin(fa_14_cout), .a(a14), .b(b14), .s(s14), .Cout(fa_15_cout));
  FA fa_16 (.cin(fa_15_cout), .a(a15), .b(b15), .s(s15), .Cout(cout));
endmodule

module FA (
  input  cin,
  input  a,
  input  b,
  output s,
  output Cout
);

  wire and_1_out, and_2_out, xor_1_out;

  xor xor_1 (xor_1_out, a, b);
  xor xor_2 (s, cin, xor_1_out);
  and and_1 (and_1_out, cin, xor_1_out);
  and and_2 (and_2_out, a, b);
  or or_1 (Cout, and_1_out, and_2_out);
endmodule

module B16bitShiftLeft (
  input  Clock,
  input  s0,
  input  s1,
  input  d0,
  input  d1,
  input  d2,
  input  d3,
  input  d4,
  input  d5,
  input  d6,
  input  d7,
  input  d8,
  input  d9,
  input  d10,
  input  d11,
  input  d12,
  input  d13,
  input  d14,
  input  d15,
  output q0,
  output q1,
  output q2,
  output q3,
  output q4,
  output q5,
  output q6,
  output q7,
  output q8,
  output q9,
  output q10,
  output q11,
  output q12,
  output q13,
  output q14,
  output q15
);

  wire multiplexer_1_out, multiplexer_2_out, multiplexer_3_out, multiplexer_4_out, multiplexer_5_out,
       multiplexer_6_out, multiplexer_7_out, multiplexer_8_out, multiplexer_9_out, multiplexer_10_out,
       multiplexer_11_out, multiplexer_12_out, multiplexer_13_out, multiplexer_14_out, multiplexer_15_out,
       multiplexer_16_out;

  Multiplexer #(.select(2)) multiplexer_1 (
    .in0(q15), .in1(d15), .in2(q14), .out(multiplexer_1_out), .sel({s1, s0}));  // open: in3
  D_Flip_Flop d_ff_1 (.D(multiplexer_1_out), .clk(Clock), .Q(q15));  // open: Qn, preset, reset
  Multiplexer #(.select(2)) multiplexer_2 (
    .in0(q14), .in1(d14), .in2(q13), .out(multiplexer_2_out), .sel({s1, s0}));  // open: in3
  D_Flip_Flop d_ff_2 (.D(multiplexer_2_out), .clk(Clock), .Q(q14));  // open: Qn, preset, reset
  Multiplexer #(.select(2)) multiplexer_3 (
    .in0(q13), .in1(d13), .in2(q12), .out(multiplexer_3_out), .sel({s1, s0}));  // open: in3
  D_Flip_Flop d_ff_3 (.D(multiplexer_3_out), .clk(Clock), .Q(q13));  // open: Qn, preset, reset
  Multiplexer #(.select(2)) multiplexer_4 (
    .in0(q12), .in1(d12), .in2(q11), .out(multiplexer_4_out), .sel({s1, s0}));  // open: in3
  D_Flip_Flop d_ff_4 (.D(multiplexer_4_out), .clk(Clock), .Q(q12));  // open: Qn, preset, reset
  Multiplexer #(.select(2)) multiplexer_5 (
    .in0(q11), .in1(d11), .in2(q10), .out(multiplexer_5_out), .sel({s1, s0}));  // open: in3
  D_Flip_Flop d_ff_5 (.D(multiplexer_5_out), .clk(Clock), .Q(q11));  // open: Qn, preset, reset
  Multiplexer #(.select(2)) multiplexer_6 (
    .in0(q10), .in1(d10), .in2(q9), .out(multiplexer_6_out), .sel({s1, s0}));  // open: in3
  D_Flip_Flop d_ff_6 (.D(multiplexer_6_out), .clk(Clock), .Q(q10));  // open: Qn, preset, reset
  Multiplexer #(.select(2)) multiplexer_7 (
    .in0(q9), .in1(d9), .in2(q8), .out(multiplexer_7_out), .sel({s1, s0}));  // open: in3
  D_Flip_Flop d_ff_7 (.D(multiplexer_7_out), .clk(Clock), .Q(q9));  // open: Qn, preset, reset
  Multiplexer #(.select(2)) multiplexer_8 (
    .in0(q8), .in1(d8), .in2(q7), .out(multiplexer_8_out), .sel({s1, s0}));  // open: in3
  D_Flip_Flop d_ff_8 (.D(multiplexer_8_out), .clk(Clock), .Q(q8));  // open: Qn, preset, reset
  Multiplexer #(.select(2)) multiplexer_9 (
    .in0(q7), .in1(d7), .in2(q6), .out(multiplexer_9_out), .sel({s1, s0}));  // open: in3
  D_Flip_Flop d_ff_9 (.D(multiplexer_9_out), .clk(Clock), .Q(q7));  // open: Qn, preset, reset
  Multiplexer #(.select(2)) multiplexer_10 (
    .in0(q6), .in1(d6), .in2(q5), .out(multiplexer_10_out), .sel({s1, s0}));  // open: in3
  D_Flip_Flop d_ff_10 (.D(multiplexer_10_out), .clk(Clock), .Q(q6));  // open: Qn, preset, reset
  Multiplexer #(.select(2)) multiplexer_11 (
    .in0(q5), .in1(d5), .in2(q4), .out(multiplexer_11_out), .sel({s1, s0}));  // open: in3
  D_Flip_Flop d_ff_11 (.D(multiplexer_11_out), .clk(Clock), .Q(q5));  // open: Qn, preset, reset
  Multiplexer #(.select(2)) multiplexer_12 (
    .in0(q4), .in1(d4), .in2(q3), .out(multiplexer_12_out), .sel({s1, s0}));  // open: in3
  D_Flip_Flop d_ff_12 (.D(multiplexer_12_out), .clk(Clock), .Q(q4));  // open: Qn, preset, reset
  Multiplexer #(.select(2)) multiplexer_13 (
    .in0(q3), .in1(d3), .in2(q2), .out(multiplexer_13_out), .sel({s1, s0}));  // open: in3
  D_Flip_Flop d_ff_13 (.D(multiplexer_13_out), .clk(Clock), .Q(q3));  // open: Qn, preset, reset
  Multiplexer #(.select(2)) multiplexer_14 (
    .in0(q2), .in1(d2), .in2(q1), .out(multiplexer_14_out), .sel({s1, s0}));  // open: in3
  D_Flip_Flop d_ff_14 (.D(multiplexer_14_out), .clk(Clock), .Q(q2));  // open: Qn, preset, reset
  Multiplexer #(.select(2)) multiplexer_15 (
    .in0(q1), .in1(d1), .in2(q0), .out(multiplexer_15_out), .sel({s1, s0}));  // open: in3
  D_Flip_Flop d_ff_15 (.D(multiplexer_15_out), .clk(Clock), .Q(q1));  // open: Qn, preset, reset
  Multiplexer #(.select(2)) multiplexer_16 (
    .in0(q0), .in1(d0), .in2(1'b0), .out(multiplexer_16_out), .sel({s1, s0}));  // open: in3
  D_Flip_Flop d_ff_16 (.D(multiplexer_16_out), .clk(Clock), .Q(q0));  // open: Qn, preset, reset
endmodule

module B8bitShiftRight (
  input  Clock,
  input  s0,
  input  s1,
  input  d0,
  input  d1,
  input  d2,
  input  d3,
  input  d4,
  input  d5,
  input  d6,
  input  d7,
  output q0,
  output q1,
  output q2,
  output q3,
  output q4,
  output q5,
  output q6,
  output q7
);

  wire multiplexer_1_out, multiplexer_2_out, multiplexer_3_out, multiplexer_4_out, multiplexer_5_out,
       multiplexer_6_out, multiplexer_7_out, multiplexer_8_out;

  Multiplexer #(.select(2)) multiplexer_1 (
    .in0(q7), .in1(d7), .in2(1'b0), .out(multiplexer_1_out), .sel({s1, s0}));  // open: in3
  D_Flip_Flop d_ff_1 (.D(multiplexer_1_out), .clk(Clock), .Q(q7));  // open: Qn, preset, reset
  Multiplexer #(.select(2)) multiplexer_2 (
    .in0(q6), .in1(d6), .in2(q7), .out(multiplexer_2_out), .sel({s1, s0}));  // open: in3
  D_Flip_Flop d_ff_2 (.D(multiplexer_2_out), .clk(Clock), .Q(q6));  // open: Qn, preset, reset
  Multiplexer #(.select(2)) multiplexer_3 (
    .in0(q5), .in1(d5), .in2(q6), .out(multiplexer_3_out), .sel({s1, s0}));  // open: in3
  D_Flip_Flop d_ff_3 (.D(multiplexer_3_out), .clk(Clock), .Q(q5));  // open: Qn, preset, reset
  Multiplexer #(.select(2)) multiplexer_4 (
    .in0(q4), .in1(d4), .in2(q5), .out(multiplexer_4_out), .sel({s1, s0}));  // open: in3
  D_Flip_Flop d_ff_4 (.D(multiplexer_4_out), .clk(Clock), .Q(q4));  // open: Qn, preset, reset
  Multiplexer #(.select(2)) multiplexer_5 (
    .in0(q3), .in1(d3), .in2(q4), .out(multiplexer_5_out), .sel({s1, s0}));  // open: in3
  D_Flip_Flop d_ff_5 (.D(multiplexer_5_out), .clk(Clock), .Q(q3));  // open: Qn, preset, reset
  Multiplexer #(.select(2)) multiplexer_6 (
    .in0(q2), .in1(d2), .in2(q3), .out(multiplexer_6_out), .sel({s1, s0}));  // open: in3
  D_Flip_Flop d_ff_6 (.D(multiplexer_6_out), .clk(Clock), .Q(q2));  // open: Qn, preset, reset
  Multiplexer #(.select(2)) multiplexer_7 (
    .in0(q1), .in1(d1), .in2(q2), .out(multiplexer_7_out), .sel({s1, s0}));  // open: in3
  D_Flip_Flop d_ff_7 (.D(multiplexer_7_out), .clk(Clock), .Q(q1));  // open: Qn, preset, reset
  Multiplexer #(.select(2)) multiplexer_8 (
    .in0(q0), .in1(d0), .in2(q1), .out(multiplexer_8_out), .sel({s1, s0}));  // open: in3
  D_Flip_Flop d_ff_8 (.D(multiplexer_8_out), .clk(Clock), .Q(q0));  // open: Qn, preset, reset
endmodule

module finalProject (
  input  InitialLoad,
  input  [7:0] Multiplicand,
  input  [7:0] Multiplier,
  input  Clock,
  output [15:0] ProductInBinary,
  output [19:0] Dicimal,
  output IsNegetive,
  output [4:0] counter
);

  wire and_1_out, not_1_out, or_1_out, shift_register_1_p2, shift_register_1_p17, shift_register_1_p18,
       shift_register_1_p19, shift_register_1_p20, shift_register_1_p21, shift_register_1_p22,
       shift_register_1_p23, shift_register_1_p24, shift_register_1_p25, shift_register_1_p26,
       shift_register_1_p27, shift_register_1_p28, undriven, undriven_2, undriven_3, undriven_4,
       unsignedmultiplier_1_finished;
  wire [7:0] eightbitstc_1_c, eightbitstc_2_c;
  wire [15:0] multiplexer_1_out;

  eightBitsTC eightbitstc_1 (
    .a(Multiplicand[0]), .a1(Multiplicand[1]), .a2(Multiplicand[2]), .a3(Multiplicand[3]),
    .a4(Multiplicand[4]), .a5(Multiplicand[5]), .a6(Multiplicand[6]), .a7(Multiplicand[7]),
    .c(eightbitstc_1_c[0]), .c1(eightbitstc_1_c[1]), .c2(eightbitstc_1_c[2]), .c3(eightbitstc_1_c[3]),
    .c4(eightbitstc_1_c[4]), .c5(eightbitstc_1_c[5]), .c6(eightbitstc_1_c[6]), .c7(eightbitstc_1_c[7]));
  eightBitsTC eightbitstc_2 (
    .a(Multiplier[0]), .a1(Multiplier[1]), .a2(Multiplier[2]), .a3(Multiplier[3]), .a4(Multiplier[4]),
    .a5(Multiplier[5]), .a6(Multiplier[6]), .a7(Multiplier[7]), .c(eightbitstc_2_c[0]),
    .c1(eightbitstc_2_c[1]), .c2(eightbitstc_2_c[2]), .c3(eightbitstc_2_c[3]), .c4(eightbitstc_2_c[4]),
    .c5(eightbitstc_2_c[5]), .c6(eightbitstc_2_c[6]), .c7(eightbitstc_2_c[7]));
  xor xor_1 (IsNegetive, Multiplier[7], Multiplicand[7]);
  unsignedMultiplier unsignedmultiplier_1 (
    .Multiplier(eightbitstc_2_c), .Multiplicand(eightbitstc_1_c), .Clock(Clock),
    .Initial_constant(InitialLoad), .Product(ProductInBinary), .Finished(unsignedmultiplier_1_finished));
  Multiplexer #(.width(16)) multiplexer_1 (
    .in0({16{1'b0}}), .in1(ProductInBinary), .out(multiplexer_1_out), .sel(unsignedmultiplier_1_finished));
  and and_1 (and_1_out, not_1_out, unsignedmultiplier_1_finished);
  // Shift_Register #(.length(16)) shift_register_1: pin names not known; wires that end beside it: and_1_out, shift_register_1_p2, Clock, 1'b0, multiplexer_1_out[0], multiplexer_1_out[1], multiplexer_1_out[2], multiplexer_1_out[3], multiplexer_1_out[4], multiplexer_1_out[5], multiplexer_1_out[6], multiplexer_1_out[7], multiplexer_1_out[8], multiplexer_1_out[9], multiplexer_1_out[10], multiplexer_1_out[11], shift_register_1_p17, shift_register_1_p18, shift_register_1_p19, shift_register_1_p20, shift_register_1_p21, shift_register_1_p22, shift_register_1_p23, shift_register_1_p24, shift_register_1_p25, shift_register_1_p26, shift_register_1_p27, shift_register_1_p28
  or or_1 (or_1_out, shift_register_1_p17, shift_register_1_p18, shift_register_1_p19, shift_register_1_p20, shift_register_1_p21, shift_register_1_p22, shift_register_1_p23, shift_register_1_p24, shift_register_1_p25, shift_register_1_p26, shift_register_1_p27, shift_register_1_p28, undriven, undriven_2, undriven_3, undriven_4);
  not not_1 (not_1_out, or_1_out);
  double_dabble double_dabble_1 (
    .L(undriven_4), .clk(Clock), .initial_constant(InitialLoad), .start_counter(or_1_out), .a0(Dicimal[0]),
    .a1(Dicimal[1]), .a2(Dicimal[2]), .a3(Dicimal[3]), .a4(Dicimal[4]), .a5(Dicimal[5]), .a6(Dicimal[6]),
    .a7(Dicimal[7]), .a8(Dicimal[8]), .a9(Dicimal[9]), .a10(Dicimal[10]), .a11(Dicimal[11]),
    .a12(Dicimal[12]), .a13(Dicimal[13]), .a14(Dicimal[14]), .a15(Dicimal[15]), .a16(Dicimal[16]),
    .a17(Dicimal[17]), .a18(Dicimal[18]), .a19(Dicimal[19]), .enable(shift_register_1_p2), .cntr(counter));

  // Notes on the sheet:
  //   no number
endmodule

module double_dabble (
  input  L,
  input  clk,
  input  initial_constant,
  input  start_counter,
  output a0,
  output a1,
  output a2,
  output a3,
  output a4,
  output a5,
  output a6,
  output a7,
  output a8,
  output a9,
  output a10,
  output a11,
  output a12,
  output a13,
  output a14,
  output a15,
  output a16,
  output a17,
  output a18,
  output a19,
  output enable,
  output [4:0] cntr
);

  wire and_1_out, and_2_out, and_3_out, and_4_out, and_6_out, and_7_out, and_8_out, and_10_out, and_11_out,
       and_12_out, and_14_out, and_15_out, and_16_out, and_18_out, and_19_out, and_20_out, and_22_out,
       d_ff_1_q, d_ff_1_qn, d_ff_2_q, d_ff_6_qn, d_ff_7_qn, d_ff_10_qn, d_ff_11_qn, d_ff_14_qn, d_ff_15_qn,
       d_ff_18_qn, d_ff_19_qn, d_ff_22_qn, d_ff_23_qn, multiplexer_1_out, multiplexer_2_out,
       multiplexer_3_out, multiplexer_4_out, multiplexer_5_out, multiplexer_6_out, multiplexer_7_out,
       multiplexer_8_out, multiplexer_9_out, multiplexer_10_out, multiplexer_11_out, multiplexer_12_out,
       multiplexer_13_out, multiplexer_14_out, multiplexer_15_out, multiplexer_16_out, multiplexer_17_out,
       multiplexer_18_out, multiplexer_19_out, multiplexer_20_out, not_1_out, not_2_out, not_3_out,
       not_4_out, not_5_out, not_6_out, not_7_out, not_8_out, not_9_out, or_1_out, or_2_out, or_3_out,
       or_4_out, or_5_out, or_6_out, or_7_out, or_8_out, or_9_out, or_10_out, or_11_out, or_12_out, t_ff_1_q;
  wire [1:1] and_5_out, and_9_out, and_13_out, and_17_out, and_21_out;
  wire [3:0] adder_1_out, adder_2_out, adder_3_out, adder_4_out, adder_5_out;

  T_Flip_Flop t_ff_1 (.Q(t_ff_1_q), .preset(start_counter));  // open: T, clk, Qn, reset
  D_Flip_Flop d_ff_1 (.D(enable), .clk(clk), .Q(d_ff_1_q), .Qn(d_ff_1_qn));  // open: preset, reset
  D_Flip_Flop d_ff_2 (.D(d_ff_1_q), .clk(clk), .Q(d_ff_2_q));  // open: Qn, preset, reset
  D_Flip_Flop #(.trigger("falling")) d_ff_3 (
    .D(or_1_out), .clk(clk), .Q(enable), .preset(initial_constant), .reset(cntr[4]));  // open: Qn
  and and_1 (and_1_out, d_ff_2_q, d_ff_1_qn);
  or or_1 (or_1_out, and_2_out, and_1_out);
  D_Flip_Flop d_ff_4 (.D(multiplexer_1_out), .clk(clk), .Q(a19));  // open: Qn, preset, reset
  Multiplexer multiplexer_1 (.in0(adder_1_out[3]), .in1(a18), .out(multiplexer_1_out), .sel(enable));
  and and_2 (and_2_out, not_1_out, not_7_out, not_9_out, not_8_out, not_4_out);
  and and_3 (and_3_out, a18, d_ff_6_qn, a16);
  not not_1 (not_1_out, or_4_out);
  not not_2 (not_2_out, enable);
  or or_2 (or_2_out, and_3_out, and_6_out, and_4_out);
  D_Flip_Flop d_ff_5 (.D(multiplexer_2_out), .clk(clk), .Q(a18));  // open: Qn, preset, reset
  Multiplexer multiplexer_2 (.in0(adder_1_out[2]), .in1(a17), .out(multiplexer_2_out), .sel(enable));
  not not_3 (not_3_out, t_ff_1_q);
  or or_3 (or_3_out, not_2_out, not_3_out, cntr[4]);
  and and_4 (and_4_out, a18, a17, d_ff_7_qn);
  not not_4 (not_4_out, or_12_out);
  Counter #(.max('h1f), .width(5)) counter_1 (.count(not_5_out), .clk(clk), .Q(cntr));  // open: clr, load, up, D, carry
  not not_5 (not_5_out, or_3_out);
  or or_4 (or_4_out, a19, or_2_out);
  not not_6 (not_6_out, cntr[4]);
  not not_7 (not_7_out, or_6_out);
  not not_8 (not_8_out, or_10_out);
  D_Flip_Flop d_ff_6 (.D(multiplexer_3_out), .clk(clk), .Q(a17), .Qn(d_ff_6_qn));  // open: preset, reset
  Multiplexer multiplexer_3 (.in0(adder_1_out[1]), .in1(a16), .out(multiplexer_3_out), .sel(enable));
  and and_5 (and_5_out[1], or_4_out, not_6_out);
  and and_6 (and_6_out, a18, a17, a16);
  Adder #(.width(4)) adder_1 (
    .a({a19, a18, a17, a16}), .b({2'b00, {2{and_5_out[1]}}}), .out(adder_1_out));  // open: cin, cout
  not not_9 (not_9_out, or_8_out);
  Multiplexer multiplexer_4 (.in0(adder_1_out[0]), .in1(a15), .out(multiplexer_4_out), .sel(enable));
  D_Flip_Flop d_ff_7 (.D(multiplexer_4_out), .clk(clk), .Q(a16), .Qn(d_ff_7_qn));  // open: preset, reset
  D_Flip_Flop d_ff_8 (.D(multiplexer_5_out), .clk(clk), .Q(a15));  // open: Qn, preset, reset
  Multiplexer multiplexer_5 (.in0(adder_2_out[3]), .in1(a14), .out(multiplexer_5_out), .sel(enable));
  and and_7 (and_7_out, a14, d_ff_10_qn, a12);
  or or_5 (or_5_out, and_7_out, and_10_out, and_8_out);
  Multiplexer multiplexer_6 (.in0(adder_2_out[2]), .in1(a13), .out(multiplexer_6_out), .sel(enable));
  D_Flip_Flop d_ff_9 (.D(multiplexer_6_out), .clk(clk), .Q(a14));  // open: Qn, preset, reset
  and and_8 (and_8_out, a14, a13, d_ff_11_qn);
  or or_6 (or_6_out, a15, or_5_out);
  D_Flip_Flop d_ff_10 (.D(multiplexer_7_out), .clk(clk), .Q(a13), .Qn(d_ff_10_qn));  // open: preset, reset
  Multiplexer multiplexer_7 (.in0(adder_2_out[1]), .in1(a12), .out(multiplexer_7_out), .sel(enable));
  and and_9 (and_9_out[1], or_6_out, not_6_out);
  and and_10 (and_10_out, a14, a13, a12);
  Adder #(.width(4)) adder_2 (
    .a({a15, a14, a13, a12}), .b({2'b00, {2{and_9_out[1]}}}), .out(adder_2_out));  // open: cin, cout
  D_Flip_Flop d_ff_11 (.D(multiplexer_8_out), .clk(clk), .Q(a12), .Qn(d_ff_11_qn));  // open: preset, reset
  Multiplexer multiplexer_8 (.in0(adder_2_out[0]), .in1(a11), .out(multiplexer_8_out), .sel(enable));
  D_Flip_Flop d_ff_12 (.D(multiplexer_9_out), .clk(clk), .Q(a11));  // open: Qn, preset, reset
  Multiplexer multiplexer_9 (.in0(adder_3_out[3]), .in1(a10), .out(multiplexer_9_out), .sel(enable));
  and and_11 (and_11_out, a10, d_ff_14_qn, a8);
  or or_7 (or_7_out, and_11_out, and_14_out, and_12_out);
  D_Flip_Flop d_ff_13 (.D(multiplexer_10_out), .clk(clk), .Q(a10));  // open: Qn, preset, reset
  Multiplexer multiplexer_10 (.in0(adder_3_out[2]), .in1(a9), .out(multiplexer_10_out), .sel(enable));
  and and_12 (and_12_out, a10, a9, d_ff_15_qn);
  or or_8 (or_8_out, a11, or_7_out);
  D_Flip_Flop d_ff_14 (.D(multiplexer_11_out), .clk(clk), .Q(a9), .Qn(d_ff_14_qn));  // open: preset, reset
  Multiplexer multiplexer_11 (.in0(adder_3_out[1]), .in1(a8), .out(multiplexer_11_out), .sel(enable));
  and and_13 (and_13_out[1], or_8_out, not_6_out);
  and and_14 (and_14_out, a10, a9, a8);
  Adder #(.width(4)) adder_3 (
    .a({a11, a10, a9, a8}), .b({2'b00, {2{and_13_out[1]}}}), .out(adder_3_out));  // open: cin, cout
  D_Flip_Flop d_ff_15 (.D(multiplexer_12_out), .clk(clk), .Q(a8), .Qn(d_ff_15_qn));  // open: preset, reset
  Multiplexer multiplexer_12 (.in0(adder_3_out[0]), .in1(a7), .out(multiplexer_12_out), .sel(enable));
  D_Flip_Flop d_ff_16 (.D(multiplexer_13_out), .clk(clk), .Q(a7));  // open: Qn, preset, reset
  Multiplexer multiplexer_13 (.in0(adder_4_out[3]), .in1(a6), .out(multiplexer_13_out), .sel(enable));
  and and_15 (and_15_out, a6, d_ff_18_qn, a4);
  or or_9 (or_9_out, and_15_out, and_18_out, and_16_out);
  D_Flip_Flop d_ff_17 (.D(multiplexer_14_out), .clk(clk), .Q(a6));  // open: Qn, preset, reset
  Multiplexer multiplexer_14 (.in0(adder_4_out[2]), .in1(a5), .out(multiplexer_14_out), .sel(enable));
  and and_16 (and_16_out, a6, a5, d_ff_19_qn);
  or or_10 (or_10_out, a7, or_9_out);
  D_Flip_Flop d_ff_18 (.D(multiplexer_15_out), .clk(clk), .Q(a5), .Qn(d_ff_18_qn));  // open: preset, reset
  Multiplexer multiplexer_15 (.in0(adder_4_out[1]), .in1(a4), .out(multiplexer_15_out), .sel(enable));
  and and_17 (and_17_out[1], or_10_out, not_6_out);
  and and_18 (and_18_out, a6, a5, a4);
  Adder #(.width(4)) adder_4 (
    .a({a7, a6, a5, a4}), .b({2'b00, {2{and_17_out[1]}}}), .out(adder_4_out));  // open: cin, cout
  D_Flip_Flop d_ff_19 (.D(multiplexer_16_out), .clk(clk), .Q(a4), .Qn(d_ff_19_qn));  // open: preset, reset
  Multiplexer multiplexer_16 (.in0(adder_4_out[0]), .in1(a3), .out(multiplexer_16_out), .sel(enable));
  D_Flip_Flop d_ff_20 (.D(multiplexer_17_out), .clk(clk), .Q(a3));  // open: Qn, preset, reset
  Multiplexer multiplexer_17 (.in0(adder_5_out[3]), .in1(a2), .out(multiplexer_17_out), .sel(enable));
  and and_19 (and_19_out, a2, d_ff_22_qn, a0);
  or or_11 (or_11_out, and_19_out, and_22_out, and_20_out);
  D_Flip_Flop d_ff_21 (.D(multiplexer_18_out), .clk(clk), .Q(a2));  // open: Qn, preset, reset
  Multiplexer multiplexer_18 (.in0(adder_5_out[2]), .in1(a1), .out(multiplexer_18_out), .sel(enable));
  and and_20 (and_20_out, a2, a1, d_ff_23_qn);
  or or_12 (or_12_out, a3, or_11_out);
  Multiplexer multiplexer_19 (.in0(adder_5_out[1]), .in1(a0), .out(multiplexer_19_out), .sel(enable));
  D_Flip_Flop d_ff_22 (.D(multiplexer_19_out), .clk(clk), .Q(a1), .Qn(d_ff_22_qn));  // open: preset, reset
  and and_21 (and_21_out[1], or_12_out, not_6_out);
  and and_22 (and_22_out, a2, a1, a0);
  Adder #(.width(4)) adder_5 (
    .a({a3, a2, a1, a0}), .b({2'b00, {2{and_21_out[1]}}}), .out(adder_5_out));  // open: cin, cout
  D_Flip_Flop d_ff_23 (.D(multiplexer_20_out), .clk(clk), .Q(a0), .Qn(d_ff_23_qn));  // open: preset, reset
  Multiplexer multiplexer_20 (.in0(adder_5_out[0]), .in1(L), .out(multiplexer_20_out), .sel(enable));
endmodule

module A_segment (
  input  a,
  input  b,
  input  c,
  input  d,
  output x
);

  wire and_1_out, and_2_out, not_1_out, not_2_out, or_1_out, or_2_out;

  not not_1 (not_1_out, b);
  not not_2 (not_2_out, d);
  and and_1 (and_1_out, not_1_out, not_2_out);
  and and_2 (and_2_out, b, d);
  or or_1 (or_1_out, and_1_out, c);
  or or_2 (or_2_out, and_2_out, a);
  or or_3 (x, or_1_out, or_2_out);
endmodule

module B_segment (
  input  a,
  input  b,
  input  c,
  input  d,
  output x
);

  wire and_1_out, and_2_out, not_1_out, not_2_out, not_3_out, or_1_out;

  not not_1 (not_1_out, b);
  not not_2 (not_2_out, c);
  not not_3 (not_3_out, d);
  and and_1 (and_1_out, not_2_out, not_3_out);
  or or_1 (or_1_out, not_1_out, and_1_out);
  and and_2 (and_2_out, c, d);
  or or_2 (x, or_1_out, and_2_out);
endmodule

module C_segment (
  input  a,
  input  b,
  input  c,
  input  d,
  output x
);

  wire not_1_out, or_1_out;

  not not_1 (not_1_out, c);
  or or_1 (or_1_out, not_1_out, d);
  or or_2 (x, or_1_out, b);
endmodule

module D_segment (
  input  a,
  input  b,
  input  c,
  input  d,
  output x
);

  wire and_1_out, and_2_out, and_3_out, and_4_out, and_5_out, not_1_out, not_2_out, not_3_out, or_1_out,
       or_2_out, or_4_out;

  not not_1 (not_1_out, b);
  not not_2 (not_2_out, c);
  not not_3 (not_3_out, d);
  and and_1 (and_1_out, not_1_out, not_3_out);
  and and_2 (and_2_out, not_1_out, c);
  and and_3 (and_3_out, b, not_2_out);
  or or_1 (or_1_out, and_1_out, and_2_out);
  and and_4 (and_4_out, and_3_out, d);
  and and_5 (and_5_out, c, not_3_out);
  or or_2 (or_2_out, or_1_out, and_4_out);
  or or_3 (x, or_2_out, or_4_out);
  or or_4 (or_4_out, and_5_out, a);
endmodule

module E_segment (
  input  a,
  input  b,
  input  c,
  input  d,
  output x
);

  wire and_1_out, and_2_out, not_1_out, not_2_out;

  not not_1 (not_1_out, b);
  not not_2 (not_2_out, d);
  and and_1 (and_1_out, not_1_out, not_2_out);
  and and_2 (and_2_out, c, not_2_out);
  or or_1 (x, and_1_out, and_2_out);
endmodule

module F_segment (
  input  a,
  input  b,
  input  c,
  input  d,
  output x
);

  wire and_1_out, and_2_out, and_3_out, not_1_out, not_2_out;

  not not_1 (not_1_out, c);
  not not_2 (not_2_out, d);
  and and_1 (and_1_out, not_1_out, not_2_out);
  and and_2 (and_2_out, b, not_1_out);
  and and_3 (and_3_out, b, not_2_out);
  or or_1 (x, and_1_out, and_2_out, and_3_out, a);
endmodule

module G_segment (
  input  a,
  input  b,
  input  c,
  input  d,
  output x
);

  wire and_1_out, and_2_out, and_3_out, not_1_out, not_2_out, not_3_out, or_1_out, or_2_out;

  not not_1 (not_1_out, b);
  not not_2 (not_2_out, c);
  not not_3 (not_3_out, d);
  and and_1 (and_1_out, not_1_out, c);
  and and_2 (and_2_out, b, not_2_out);
  and and_3 (and_3_out, c, not_3_out);
  or or_1 (or_1_out, and_1_out, and_2_out);
  or or_2 (or_2_out, a, and_3_out);
  or or_3 (x, or_1_out, or_2_out);
endmodule

module Decoder_7_segment (
  input  d,
  input  c,
  input  b,
  input  a,
  output A_seg,
  output B_seg,
  output C_seg,
  output D_seg,
  output E_seg,
  output F_seg,
  output G_seg
);

  A_segment a_segment_1 (.a(a), .b(b), .c(c), .d(d), .x(A_seg));
  B_segment b_segment_1 (.a(a), .b(b), .c(c), .d(d), .x(B_seg));
  C_segment c_segment_1 (.a(a), .b(b), .c(c), .d(d), .x(C_seg));
  D_segment d_segment_1 (.a(a), .b(b), .c(c), .d(d), .x(D_seg));
  E_segment e_segment_1 (.a(a), .b(b), .c(c), .d(d), .x(E_seg));
  F_segment f_segment_1 (.a(a), .b(b), .c(c), .d(d), .x(F_seg));
  G_segment g_segment_1 (.a(a), .b(b), .c(c), .d(d), .x(G_seg));
endmodule

module eightBitsTC (
  input  a,
  input  a1,
  input  a2,
  input  a3,
  input  a4,
  input  a5,
  input  a6,
  input  a7,
  output c,
  output c1,
  output c2,
  output c3,
  output c4,
  output c5,
  output c6,
  output c7
);

  wire adder_1_cout, adder_1_out, adder_2_cout, adder_2_out, adder_3_cout, adder_3_out, adder_4_cout,
       adder_4_out, adder_5_cout, adder_5_out, adder_6_cout, adder_6_out, adder_7_cout, adder_7_out,
       adder_8_cout, adder_8_out, not_1_out, not_2_out, not_3_out, not_4_out, not_5_out, not_6_out,
       not_7_out, not_8_out;

  not not_1 (not_1_out, a7);
  Adder #(.width(1)) adder_1 (.a(not_1_out), .b(1'b0), .out(adder_1_out), .cin(adder_2_cout), .cout(adder_1_cout));
  Multiplexer multiplexer_1 (.in0(a7), .in1(adder_1_out), .out(c7), .sel(a7));
  not not_2 (not_2_out, a6);
  Adder #(.width(1)) adder_2 (.a(not_2_out), .b(1'b0), .out(adder_2_out), .cin(adder_3_cout), .cout(adder_2_cout));
  Multiplexer multiplexer_2 (.in0(a6), .in1(adder_2_out), .out(c6), .sel(a7));
  not not_3 (not_3_out, a5);
  Adder #(.width(1)) adder_3 (.a(not_3_out), .b(1'b0), .out(adder_3_out), .cin(adder_4_cout), .cout(adder_3_cout));
  Multiplexer multiplexer_3 (.in0(a5), .in1(adder_3_out), .out(c5), .sel(a7));
  not not_4 (not_4_out, a4);
  Adder #(.width(1)) adder_4 (.a(not_4_out), .b(1'b0), .out(adder_4_out), .cin(adder_5_cout), .cout(adder_4_cout));
  Multiplexer multiplexer_4 (.in0(a4), .in1(adder_4_out), .out(c4), .sel(a7));
  not not_5 (not_5_out, a3);
  Adder #(.width(1)) adder_5 (.a(not_5_out), .b(1'b0), .out(adder_5_out), .cin(adder_6_cout), .cout(adder_5_cout));
  Multiplexer multiplexer_5 (.in0(a3), .in1(adder_5_out), .out(c3), .sel(a7));
  not not_6 (not_6_out, a2);
  Adder #(.width(1)) adder_6 (.a(not_6_out), .b(1'b0), .out(adder_6_out), .cin(adder_7_cout), .cout(adder_6_cout));
  Multiplexer multiplexer_6 (.in0(a2), .in1(adder_6_out), .out(c2), .sel(a7));
  not not_7 (not_7_out, a1);
  Adder #(.width(1)) adder_7 (.a(not_7_out), .b(1'b0), .out(adder_7_out), .cin(adder_8_cout), .cout(adder_7_cout));
  Multiplexer multiplexer_7 (.in0(a1), .in1(adder_7_out), .out(c1), .sel(a7));
  not not_8 (not_8_out, a);
  Adder #(.width(1)) adder_8 (.a(not_8_out), .b(1'b0), .out(adder_8_out), .cin(1'b1), .cout(adder_8_cout));
  Multiplexer multiplexer_8 (.in0(a), .in1(adder_8_out), .out(c), .sel(a7));
endmodule

module shift_left_4 (
  input  a0,
  input  a1,
  input  a2,
  input  a3,
  input  a4,
  input  a5,
  input  a6,
  input  a7,
  input  a8,
  input  a9,
  input  a10,
  input  a11,
  input  a12,
  input  a13,
  input  a14,
  input  a15,
  input  a16,
  input  a17,
  input  a18,
  input  a19,
  input  clk,
  input  load,
  input  enable,
  output o0,
  output o1,
  output o2,
  output o3,
  output o4,
  output o5,
  output o6,
  output o7,
  output o8,
  output o9,
  output o10,
  output o11,
  output o12,
  output o13,
  output o14,
  output o15,
  output o16,
  output o17,
  output o18,
  output o19
);

  wire multiplexer_1_out, multiplexer_2_out, multiplexer_3_out, multiplexer_4_out, multiplexer_5_out,
       multiplexer_6_out, multiplexer_7_out, multiplexer_8_out, multiplexer_9_out, multiplexer_10_out,
       multiplexer_11_out, multiplexer_12_out, multiplexer_13_out, multiplexer_14_out, multiplexer_15_out,
       multiplexer_16_out, multiplexer_17_out, multiplexer_18_out, multiplexer_19_out, multiplexer_20_out,
       multiplexer_21_out, multiplexer_22_out, multiplexer_23_out, multiplexer_24_out, multiplexer_25_out,
       multiplexer_26_out, multiplexer_27_out, multiplexer_28_out, multiplexer_29_out, multiplexer_30_out,
       multiplexer_31_out, multiplexer_32_out, multiplexer_33_out, multiplexer_34_out, multiplexer_35_out,
       multiplexer_36_out, multiplexer_37_out, multiplexer_38_out, multiplexer_39_out, multiplexer_40_out,
       not_1_out, not_2_out, not_3_out, not_4_out, not_5_out, not_6_out, not_7_out, not_8_out, not_9_out,
       not_10_out, not_11_out, not_12_out, not_13_out, not_14_out, not_15_out, not_16_out, not_17_out,
       not_18_out, not_19_out, not_20_out;

  Multiplexer multiplexer_1 (.in0(o19), .in1(o15), .out(multiplexer_1_out), .sel(enable));
  not not_1 (not_1_out, load);
  D_Flip_Flop d_ff_1 (.D(multiplexer_2_out), .clk(clk), .Q(o19));  // open: Qn, preset, reset
  Multiplexer multiplexer_2 (.in0(a19), .in1(multiplexer_1_out), .out(multiplexer_2_out), .sel(not_1_out));
  D_Flip_Flop d_ff_2 (.D(multiplexer_3_out), .clk(clk), .Q(o18));  // open: Qn, preset, reset
  Multiplexer multiplexer_3 (.in0(a18), .in1(multiplexer_4_out), .out(multiplexer_3_out), .sel(not_2_out));
  Multiplexer multiplexer_4 (.in0(o18), .in1(o14), .out(multiplexer_4_out), .sel(enable));
  not not_2 (not_2_out, load);
  Multiplexer multiplexer_5 (.in0(o17), .in1(o13), .out(multiplexer_5_out), .sel(enable));
  not not_3 (not_3_out, load);
  D_Flip_Flop d_ff_3 (.D(multiplexer_6_out), .clk(clk), .Q(o17));  // open: Qn, preset, reset
  Multiplexer multiplexer_6 (.in0(a17), .in1(multiplexer_5_out), .out(multiplexer_6_out), .sel(not_3_out));
  Multiplexer multiplexer_7 (.in0(o16), .in1(o12), .out(multiplexer_7_out), .sel(enable));
  D_Flip_Flop d_ff_4 (.D(multiplexer_8_out), .clk(clk), .Q(o16));  // open: Qn, preset, reset
  Multiplexer multiplexer_8 (.in0(a16), .in1(multiplexer_7_out), .out(multiplexer_8_out), .sel(not_4_out));
  not not_4 (not_4_out, load);
  D_Flip_Flop d_ff_5 (.D(multiplexer_9_out), .clk(clk), .Q(o15));  // open: Qn, preset, reset
  Multiplexer multiplexer_9 (.in0(a15), .in1(multiplexer_10_out), .out(multiplexer_9_out), .sel(not_5_out));
  Multiplexer multiplexer_10 (.in0(o15), .in1(o11), .out(multiplexer_10_out), .sel(enable));
  not not_5 (not_5_out, load);
  Multiplexer multiplexer_11 (.in0(o14), .in1(o10), .out(multiplexer_11_out), .sel(enable));
  not not_6 (not_6_out, load);
  D_Flip_Flop d_ff_6 (.D(multiplexer_12_out), .clk(clk), .Q(o14));  // open: Qn, preset, reset
  Multiplexer multiplexer_12 (.in0(a14), .in1(multiplexer_11_out), .out(multiplexer_12_out), .sel(not_6_out));
  D_Flip_Flop d_ff_7 (.D(multiplexer_13_out), .clk(clk), .Q(o13));  // open: Qn, preset, reset
  Multiplexer multiplexer_13 (.in0(a13), .in1(multiplexer_14_out), .out(multiplexer_13_out), .sel(not_7_out));
  Multiplexer multiplexer_14 (.in0(o13), .in1(o9), .out(multiplexer_14_out), .sel(enable));
  not not_7 (not_7_out, load);
  Multiplexer multiplexer_15 (.in0(a12), .in1(multiplexer_16_out), .out(multiplexer_15_out), .sel(not_8_out));
  Multiplexer multiplexer_16 (.in0(o12), .in1(o8), .out(multiplexer_16_out), .sel(enable));
  not not_8 (not_8_out, load);
  D_Flip_Flop d_ff_8 (.D(multiplexer_15_out), .clk(clk), .Q(o12));  // open: Qn, preset, reset
  Multiplexer multiplexer_17 (.in0(o11), .in1(o7), .out(multiplexer_17_out), .sel(enable));
  D_Flip_Flop d_ff_9 (.D(multiplexer_18_out), .clk(clk), .Q(o11));  // open: Qn, preset, reset
  Multiplexer multiplexer_18 (.in0(a11), .in1(multiplexer_17_out), .out(multiplexer_18_out), .sel(not_9_out));
  not not_9 (not_9_out, load);
  D_Flip_Flop d_ff_10 (.D(multiplexer_19_out), .clk(clk), .Q(o10));  // open: Qn, preset, reset
  Multiplexer multiplexer_19 (.in0(a10), .in1(multiplexer_20_out), .out(multiplexer_19_out), .sel(not_10_out));
  Multiplexer multiplexer_20 (.in0(o10), .in1(o6), .out(multiplexer_20_out), .sel(enable));
  not not_10 (not_10_out, load);
  Multiplexer multiplexer_21 (.in0(o9), .in1(o5), .out(multiplexer_21_out), .sel(enable));
  not not_11 (not_11_out, load);
  D_Flip_Flop d_ff_11 (.D(multiplexer_22_out), .clk(clk), .Q(o9));  // open: Qn, preset, reset
  Multiplexer multiplexer_22 (.in0(a9), .in1(multiplexer_21_out), .out(multiplexer_22_out), .sel(not_11_out));
  Multiplexer multiplexer_23 (.in0(o8), .in1(o4), .out(multiplexer_23_out), .sel(enable));
  D_Flip_Flop d_ff_12 (.D(multiplexer_24_out), .clk(clk), .Q(o8));  // open: Qn, preset, reset
  Multiplexer multiplexer_24 (.in0(a8), .in1(multiplexer_23_out), .out(multiplexer_24_out), .sel(not_12_out));
  not not_12 (not_12_out, load);
  D_Flip_Flop d_ff_13 (.D(multiplexer_25_out), .clk(clk), .Q(o7));  // open: Qn, preset, reset
  Multiplexer multiplexer_25 (.in0(a7), .in1(multiplexer_26_out), .out(multiplexer_25_out), .sel(not_13_out));
  Multiplexer multiplexer_26 (.in0(o7), .in1(o3), .out(multiplexer_26_out), .sel(enable));
  not not_13 (not_13_out, load);
  Multiplexer multiplexer_27 (.in0(o6), .in1(o2), .out(multiplexer_27_out), .sel(enable));
  not not_14 (not_14_out, load);
  D_Flip_Flop d_ff_14 (.D(multiplexer_28_out), .clk(clk), .Q(o6));  // open: Qn, preset, reset
  Multiplexer multiplexer_28 (.in0(a6), .in1(multiplexer_27_out), .out(multiplexer_28_out), .sel(not_14_out));
  D_Flip_Flop d_ff_15 (.D(multiplexer_29_out), .clk(clk), .Q(o5));  // open: Qn, preset, reset
  Multiplexer multiplexer_29 (.in0(a5), .in1(multiplexer_30_out), .out(multiplexer_29_out), .sel(not_15_out));
  Multiplexer multiplexer_30 (.in0(o5), .in1(o1), .out(multiplexer_30_out), .sel(enable));
  not not_15 (not_15_out, load);
  Multiplexer multiplexer_31 (.in0(a4), .in1(multiplexer_32_out), .out(multiplexer_31_out), .sel(not_16_out));
  Multiplexer multiplexer_32 (.in0(o4), .in1(o0), .out(multiplexer_32_out), .sel(enable));
  not not_16 (not_16_out, load);
  D_Flip_Flop d_ff_16 (.D(multiplexer_31_out), .clk(clk), .Q(o4));  // open: Qn, preset, reset
  Multiplexer multiplexer_33 (.in0(o3), .in1(o19), .out(multiplexer_33_out), .sel(enable));
  D_Flip_Flop d_ff_17 (.D(multiplexer_34_out), .clk(clk), .Q(o3));  // open: Qn, preset, reset
  Multiplexer multiplexer_34 (.in0(a3), .in1(multiplexer_33_out), .out(multiplexer_34_out), .sel(not_17_out));
  not not_17 (not_17_out, load);
  D_Flip_Flop d_ff_18 (.D(multiplexer_35_out), .clk(clk), .Q(o2));  // open: Qn, preset, reset
  Multiplexer multiplexer_35 (.in0(a2), .in1(multiplexer_36_out), .out(multiplexer_35_out), .sel(not_18_out));
  Multiplexer multiplexer_36 (.in0(o2), .in1(o18), .out(multiplexer_36_out), .sel(enable));
  not not_18 (not_18_out, load);
  D_Flip_Flop d_ff_19 (.D(multiplexer_37_out), .clk(clk), .Q(o1));  // open: Qn, preset, reset
  Multiplexer multiplexer_37 (.in0(a1), .in1(multiplexer_38_out), .out(multiplexer_37_out), .sel(not_19_out));
  Multiplexer multiplexer_38 (.in0(o1), .in1(o17), .out(multiplexer_38_out), .sel(enable));
  not not_19 (not_19_out, load);
  Multiplexer multiplexer_39 (.in0(o0), .in1(o16), .out(multiplexer_39_out), .sel(enable));
  not not_20 (not_20_out, load);
  D_Flip_Flop d_ff_20 (.D(multiplexer_40_out), .clk(clk), .Q(o0));  // open: Qn, preset, reset
  Multiplexer multiplexer_40 (.in0(a0), .in1(multiplexer_39_out), .out(multiplexer_40_out), .sel(not_20_out));
endmodule
